# Fritzing sketch 174proj (saved by Fritzing 0.8.0b)
breadboards: 1

parts:
  Part1 = Arduino Uno (Rev3)
  Part2 = IMU Digital Combo Board 6DOF
  roll_servo = Basic Servo
  tilt_servo = Basic Servo
  VCC1 = Battery block 9V
  Q1 = TIP120 Hi-Current Darlington Transistor
  C1 = Electrolytic Capacitor [capacitance=100µF package="200 mil [THT, electrolytic]"]
  CONN1 = USB connector [package=THT]
  VREG1 = KA78R05 Low Dropout Voltage Regulator [part_number=KA78R05 package=TO-220F-4L]  # not connected

nets:
  N1: Part1.A4/SDA, Part2.SDA
  N2: Part1.A5/SCL, Part2.SCL
  GND: Part1.GND, Part2.GND, Part2.INT0, roll_servo.gnd, tilt_servo.gnd, VCC1.-, CONN1.d-
  N3: Part1.D5_PWM, tilt_servo.pulse
  N4: Part1.D6_PWM, roll_servo.pulse
  3V3: Part1.3V3, Part2.3.3V
  VCC: roll_servo.vcc, tilt_servo.vcc, VCC1.+, Q1.BASE, C1.+
  N5: Q1.COLLECTOR, CONN1.GND, CONN1.chassis5, CONN1.chassis6
  N6: Q1.EMITTER, C1.-
